# Fritzing sketch RGBLED (saved by Fritzing 0.9.3b)
breadboards: 1

parts:
  A1 = ESP32 DevKitc V4
  LED1 = RGB LED (com. anode, rbg) [package="5 mm [THT]"]

nets:
  N1: A1.Pin_1, LED1.common_anode
  N2: A1.Pin_12, LED1.green_cathode
  N3: A1.Pin_13, LED1.red_cathode
  N4: A1.Pin_14, A1.Pin_32, A1.Pin_38
  N5: A1.Pin_15, LED1.blue_cathode

custom parts:
  ESP32 DevKitc V4: ESP32-DevKitC board with ESP32-WROOM-32 module. ESP32-DevKitC V4 is a small-sized ESP32-based development board produced by Espressif. Most of the pins on the ESP module are broken out to the pin headers on the board. The pins D0, D1, D2, D3, CMD and CLK are used internally for communication between ESP32 and SPI flash memory. They are grouped on both sides near the USB connector. Avoid using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
